# Fritzing sketch demo-circuit_winter24 (saved by Fritzing 1.0.0d)
breadboards: 1

parts:
  U1 = IC, DIP package, 40 pins [chip_label="Daisy Seed"]
  FREQ_/_P1 = Rotary Potentiometer (Small) [maximum_resistance=100kΩ knob_status=50% power=0.5W package=THT]
  MOD_/_P2 = Rotary Potentiometer (Small) [maximum_resistance=100kΩ knob_status=50% power=0.5W package=THT]
  PARAM_/_P3 = Rotary Potentiometer (Small) [maximum_resistance=100kΩ knob_status=50% power=0.5W package=THT]
  TRIG_(Internal_Pullup) = Pushbutton [package="[THT]"]
  FX_(Internal_Pullup) = Pushbutton [package="[THT]"]
  Speaker_with_Amplifier = Loudspeaker

nets:
  N1: U1.pin18, Speaker_with_Amplifier.pin1
  GND: U1.pin20, U1.pin40, FREQ_/_P1.leg2, MOD_/_P2.leg2, PARAM_/_P3.leg2, TRIG_(Internal_Pullup).Pin_3, TRIG_(Internal_Pullup).Pin_4, FX_(Internal_Pullup).Pin_3, FX_(Internal_Pullup).Pin_4, Speaker_with_Amplifier.pin2
  N2: U1.pin22, FREQ_/_P1.wiper
  N3: U1.pin23, MOD_/_P2.wiper
  N4: U1.pin24, PARAM_/_P3.wiper
  N5: U1.pin34, TRIG_(Internal_Pullup).Pin_1, TRIG_(Internal_Pullup).Pin_2
  N6: U1.pin35, FX_(Internal_Pullup).Pin_1, FX_(Internal_Pullup).Pin_2
  3.3V OUT: U1.pin38
  3.3V: FREQ_/_P1.leg1, MOD_/_P2.leg1, PARAM_/_P3.leg1
