# Fritzing sketch demodemodemo (saved by Fritzing 1.0.1rc)
breadboards: 1

parts:
  U1 = IC, DIP package, 40 pins [chip_label="Daisy Seed"]
  KNOBS_(MANY) = Rotary Potentiometer (Small) [maximum_resistance=10kΩ knob_status=50% power=0.5W package=THT]
  Speaker_with_Amplifier = Loudspeaker
  AUD_JACK = Audio Jack (TRS) 3.5mm [package="4Ucon 08780 [THT]"]
  TOUCH_SENS = MPR121 Breakout
  U2 = 74HC4067 [package=ssop24]

nets:
  N1: U1.pin14, TOUCH_SENS.SCL
  N2: U1.pin15, TOUCH_SENS.SDA
  N3: U1.pin18, Speaker_with_Amplifier.pin1, AUD_JACK.Ring
  N4: U1.pin19, AUD_JACK.Tip
  GND: U1.pin20, U1.pin40, KNOBS_(MANY).leg2, Speaker_with_Amplifier.pin2, AUD_JACK.Sleeve, TOUCH_SENS.ADDR, TOUCH_SENS.GND, U2.GND
  N5: U1.pin22, U2.COM
  N6: U1.pin29, U2.S0
  N7: U1.pin30, U2.S1
  N8: U1.pin31, U2.S2
  N9: U1.pin32, U2.S3
  3.3V OUT: U1.pin38
  3.3V: KNOBS_(MANY).leg1, TOUCH_SENS.3.3V, U2.EN, U2.VCC
  N10: KNOBS_(MANY).wiper, U2.CHAN0
