# Fritzing sketch final_layout (saved by Fritzing 1.0.1rc)
breadboards: 1

parts:
  U1 = IC, DIP package, 40 pins [chip_label="Daisy Seed"]
  Speaker_with_Amplifier = Loudspeaker
  AUD_JACK = Audio Jack (TRS) 3.5mm [package="4Ucon 08780 [THT]"]
  TOUCH_SENS = MPR121 Breakout
  U2 = 74HC4067 [package=ssop24]
  Volume = Rotary Potentiometer (Small) [maximum_resistance=100k knob_status=50% power=0.5W package=THT]
  Hall_Sensor = HALL-EFFECT [package=sc70]
  Part1 = Taiway 100-SP-X-T1 SPDT Miniature Toggle Switch [part_number=100-SP-X-T1-0-0-B1-M1 package=THT]  # not connected
  OUTPUT_SEL = SWITCH-DPDT [package=ms]

nets:
  N1: U1.pin14, TOUCH_SENS.SCL
  N2: U1.pin15, TOUCH_SENS.SDA
  N3: U1.pin18, OUTPUT_SEL.5
  N4: U1.pin19, OUTPUT_SEL.2
  GND: U1.pin20, U1.pin40, Speaker_with_Amplifier.pin2, AUD_JACK.Sleeve, TOUCH_SENS.ADDR, TOUCH_SENS.GND, U2.GND, U2.EN, Volume.leg2, Hall_Sensor.GND
  N5: U1.pin22, U2.COM
  N6: U1.pin23, Volume.wiper
  N7: U1.pin24, U2.S0
  N8: U1.pin25, U2.S1
  N9: U1.pin26, U2.S2
  N10: U1.pin27, U2.S3
  3.3V OUT: U1.pin38
  5V (BAT_CHG) IN: U1.pin39
  N11: Speaker_with_Amplifier.pin1, OUTPUT_SEL.1
  N12: AUD_JACK.Ring, OUTPUT_SEL.6
  N13: AUD_JACK.Tip, OUTPUT_SEL.4
  3.3V: TOUCH_SENS.3.3V, U2.VCC, Volume.leg1, Hall_Sensor.VCC
  N14: U2.CHAN15, Hall_Sensor.OUT
